# Fritzing sketch poject circuit (saved by Fritzing 0.9.3b)
breadboards: 2

parts:
  Part1 = Arduino Mega 2560 (Rev3)
  PIR1 = PIR sensor
  Part2 = SRF05 Ultrasonic Rangefinder
  J1 = Basic Servo
  Part3 = MQ-3 breakout
  LCD1 = LCD screen
  LED3 = LEDs [package=led10mm]
  R1 = Resistor [tolerance=±5% resistance=220 package="0402 [SMD]"]
  R2 = Resistor [tolerance=±5% resistance=220 package="0402 [SMD]"]
  LED4 = LED - 5mm [color="Red (633nm)" package="5 mm [THT]"]
  LED5 = LED - 5mm [color="Red (633nm)" package="5 mm [THT]"]
  LED6 = LED - 5mm [color="Red (633nm)" package="5 mm [THT]"]
  LED7 = LED - 5mm [color="Red (633nm)" package="5 mm [THT]"]
  LED8 = LED - 5mm [color="Red (633nm)" package="5 mm [THT]"]
  LED9 = LED - 5mm [color="Red (633nm)" package="5 mm [THT]"]
  LED10 = LED - 5mm [color="Red (633nm)" package="5 mm [THT]"]
  LED11 = LED - 5mm [color="Red (633nm)" package="5 mm [THT]"]
  LED12 = LED - 5mm [color="Red (633nm)" package="5 mm [THT]"]
  LED13 = LED - 5mm [color="Red (633nm)" package="5 mm [THT]"]
  R3 = Resistor [tolerance=±5% resistance=220 package="0402 [SMD]"]
  LED14 = Green LED - Rect 5x2x7mm [package="5x2x7 mm [THT]"]
  R4 = Resistor [tolerance=±5% resistance=220 package="1206 [SMD]"]  # not connected
  U1 = POT [package=pot_mammoth]
  J2 = Piezo Speaker

nets:
  N1: Part1.A5, Part3.AO
  N2: Part1.D20/SDA, J2.pin2
  GND: Part1.GND, PIR1.GND, Part2.GND, J1.gnd, Part3.GND, LCD1.VSS, LCD1.R/W, LCD1.LED-, R3.Pin_1, U1.S, J2.pin1
  N3: Part1.D9_PWM, J1.pulse
  VCC: Part1.5V, PIR1.VDD, Part2.VCC, J1.vcc, Part3.VCC, LCD1.VDD, U1.E
  N4: Part1.D2_PWM, LED14.anode
  N5: Part1.D3_PWM, LED3.A
  N6: Part1.D4_PWM, PIR1.SIG
  N7: Part1.D5_PWM, Part2.Trig
  N8: Part1.D6_PWM, Part2.Echo
  N9: Part1.D22, LCD1.RS
  N10: Part1.D23, LCD1.E
  N11: Part1.D24, LCD1.DB0
  N12: Part1.D25, LCD1.DB1
  N13: Part1.D26, LCD1.DB2
  N14: Part1.D27, LCD1.DB3
  N15: Part1.D28, LCD1.DB4
  N16: Part1.D29, LCD1.DB5
  N17: Part1.D30, LCD1.DB6
  N18: Part1.D31, LCD1.DB7
  N19: Part1.D44, LED8.anode
  N20: Part1.D45, LED5.anode
  N21: Part1.D46, LED6.anode
  N22: Part1.D47, LED4.anode
  N23: Part1.D48, LED9.anode
  N24: Part1.D49, LED10.anode
  N25: Part1.D50, LED11.anode
  N26: Part1.D51, LED13.anode
  N27: Part1.D52, LED12.anode
  N28: Part1.D53, LED7.anode
  N29: LCD1.V0, U1.A
  N30: R1.Pin_0, R2.Pin_0
  N31: LED4.cathode, LED5.cathode, LED6.cathode, LED7.cathode, LED8.cathode, LED9.cathode, LED10.cathode, LED11.cathode, LED12.cathode, LED13.cathode, R3.Pin_0

custom parts:
  MQ-3 breakout: Alcohol sensor is capable of detecting alcohol (ethanol) particles on itself and gives the information in digital form back to us to manipulate with it. SKU:101251 • Voltage: 5V DC • Power: max 750mW • Measurement range: 0.04-4mg/L
  Green LED - Rect 5x2x7mm: A generic rectangular green LED (~1.8V) 5mm x 2mm x 7mm

// code stored in the sketch: fritzing_code.ino
#include<Servo.h>                          //library for servo
#include<LiquidCrystal.h>                  //library for LCD display
#define pir 4
#define whiteled 3
#define greenled 2
#define trig 5
#define echo 6
#define servo_pin 9
#define buzzer 20
#define alcohol 5
Servo myservo;                             //creating servo object              
long duration=0;
float dist=0;
float distance=0;
float max_smoke = 0;
float smoke=0;
int i;
int temp=0;
unsigned long starttime,endtime;
LiquidCrystal lcd(22,23,24,25,26,27,28,29,30,31);            //creating liquidcrystal object

void setup()
{
  pinMode(pir,INPUT);
  pinMode(whiteled,OUTPUT);
  pinMode(greenled,OUTPUT);
  pinMode(trig,OUTPUT);
  pinMode(echo,INPUT);
  myservo.attach(servo_pin);                              //this says where signal pin is actually connected
  pinMode(buzzer,OUTPUT);
  pinMode(alcohol,INPUT);
  for(i=44;i<=53;i++)
  pinMode(i,OUTPUT);
  myservo.write(0);                                       //set servo to 0 position
  lcd.begin(16, 2);                                       //initialises interface to lcd screen
}

void loop() 
{
  if(digitalRead(pir) == 1)                               //checks for presence of person
  {
    lcd.clear();                                          //clears lcd screen
    lcd.setCursor(3,0);                                   //sets position in lcd screen to print
    lcd.print("WELCOME");                                 //prints in lcd screen
    check_dist();
   }
   else
   {
    digitalWrite(whiteled,LOW);
    myservo.write(0);                                     //if no person is present servo will be at initial position
   }
   
 }

void check_dist()
{
  while(digitalRead(pir)==1)
  {
    digitalWrite(whiteled,HIGH);                          //glow white led when person is present
    digitalWrite(trig,LOW);
    delayMicroseconds(2);
    digitalWrite(trig,HIGH);
    delayMicroseconds(10);
    digitalWrite(trig,LOW);
    duration = pulseIn(echo,HIGH);                        //calculates duration for switching echo pin from low to high
    dist = (duration/58.138)*0.39;                        //calc distance in inches
    distance = dist*2.54;                                 //distance in cm
    if(distance<=5)                                       //checks for distance less than 5
    {
      digitalWrite(greenled,HIGH);                        //when distance less tahn 5 glow green led
      delay(500);
      detection();
    }
    else 
    digitalWrite(greenled,LOW); 
  }
}
void detection()
{
  while(distance<=5)
  {
    lcd.clear();
    lcd.setCursor(3,0);
    lcd.print("Be Ready");
    digitalWrite(whiteled,HIGH);
    digitalWrite(trig,LOW);
    delayMicroseconds(2);
    digitalWrite(trig,HIGH);
    delayMicroseconds(10);
    digitalWrite(trig,LOW);
    duration = pulseIn(echo,HIGH);
    dist = (duration/58.138)*0.39;
    distance = dist*2.54;
    myservo.write(90); 
    tone(4,1000,500);
    starttime = millis();
    endtime = starttime;
    while((endtime-starttime)<5000)
    {
      smoke = analogRead(alcohol);
      if(smoke>temp)
      temp=smoke;
      endtime=millis();
     }
     max_smoke=temp;
     lcd.clear();
     lcd.setCursor(1,0);
     lcd.print("Sensor val=");
     lcd.setCursor(12,0);
     lcd.print(max_smoke);
     lcd.setCursor(1,1);
     lcd.print("Level =");
     if(max_smoke<30)
     {
      lcd.setCursor(9,1);
      lcd.print("1");
      digitalWrite(2,HIGH);
       for(i=44;i<=53;i++)
         digitalWrite(i,LOW);
         
     }
      if(max_smoke>=30 && max_smoke<40)
     {
      lcd.setCursor(9,1);
      lcd.print("2");
       for(i=44;i<=45;i++)
         digitalWrite(i,HIGH);
       for(i=46;i<=53;i++)
         digitalWrite(i,LOW);
     }
      if(max_smoke>=40 && max_smoke<50)
     {
      lcd.setCursor(9,1);
      lcd.print("3");
        for(i=44;i<=46;i++)
         digitalWrite(i,HIGH);
       for(i=47;i<=53;i++)
         digitalWrite(i,LOW);
     }
      if(max_smoke>=50 && max_smoke<60)
     {
      lcd.setCursor(9,1);
      lcd.print("4");
       for(i=44;i<=47;i++)
         digitalWrite(i,HIGH);
       for(i=48;i<=53;i++)
         digitalWrite(i,LOW);
     }
      if(max_smoke>=60 && max_smoke<70)
     {
      lcd.setCursor(9,1);
      lcd.print("5");
       for(i=44;i<=48;i++)
         digitalWrite(i,HIGH);
       for(i=49;i<=53;i++)
         digitalWrite(i,LOW);
     }
      if(max_smoke>=70 && max_smoke<80)
     {
      lcd.setCursor(9,1);
      lcd.print("6");
       for(i=44;i<=49;i++)
         digitalWrite(i,HIGH);
       for(i=50;i<=53;i++)
         digitalWrite(i,LOW);
     }
      if(max_smoke>=80 && max_smoke<90)
     {
      lcd.setCursor(9,1);
      lcd.print("7");
       for(i=44;i<50;i++)
         digitalWrite(i,HIGH);
       for(i=51;i<=53;i++)
         digitalWrite(i,LOW);
     }
      if(max_smoke>=90 && max_smoke<100)
     {
      lcd.setCursor(9,1);
      lcd.print("8");
       for(i=44;i<51;i++)
         digitalWrite(i,HIGH);
       for(i=52;i<=53;i++)
         digitalWrite(i,LOW);
     }
      if(max_smoke>=100 && max_smoke<110)
     {
      lcd.setCursor(9,1);
      lcd.print("9");
       for(i=44;i<=52;i++)
         digitalWrite(i,HIGH);
         digitalWrite(53,LOW);
     }
      if(max_smoke>=110)
     {
      lcd.setCursor(9,1);
      lcd.print("10");
       for(i=44;i<=53;i++)
         digitalWrite(i,HIGH);
     }
    delay(5000);
    lcd.clear();
    lcd.setCursor(3,0);
    lcd.print("Thank you");
    delay(5000);
  }
}
